# Fritzing sketch Lab_4_Diagram (saved by Fritzing 0.9.4)
breadboards: 1

parts:
  Arduino = Arduino Uno (Rev3)
  Ultrasound_Sensor = hc-sr04
  LCD_Display = LCD-16X2 [package=lcd-16x2]  # not connected
  Potentiometer = Rotary Potentiometer (Large) [maximum_resistance=100kΩ package=THT]
  LCD_Resistor = Resistor [tolerance=±5% resistance=220 package=THT]
  RGB_LED = RGB LED (com. cathode, rgb) [package="5 mm [THT]"]
  R3 = Resistor [tolerance=±5% resistance=330 package=THT]
  R4 = Resistor [tolerance=±5% resistance=330 package=THT]
  LED_Resistors = Resistor [tolerance=±5% resistance=330 package=THT]

nets:
  N1: Arduino.D8, Ultrasound_Sensor.Echo
  N2: Arduino.D9_PWM, Ultrasound_Sensor.Trig
  N3: Arduino.D11_PWM/MOSI, LED_Resistors.Pin_0
  N4: Arduino.D12/MISO, R4.Pin_0
  N5: Arduino.D13/SCK, R3.Pin_0
  GND: Arduino.GND, Ultrasound_Sensor.GND, Potentiometer.leg1, RGB_LED.common_cathode
  5V: Arduino.5V, Ultrasound_Sensor.VCC, Potentiometer.leg2, LCD_Resistor.Pin_0
  N6: RGB_LED.red_anode, LED_Resistors.Pin_1
  N7: RGB_LED.green_anode, R4.Pin_1
  N8: RGB_LED.blue_anode, R3.Pin_1
